# Fritzing sketch RemoteControlCar3_TB6612FNG-SLAVE (saved by Fritzing 0.9.3b)
breadboards: 1

parts:
  M1 = DC Motor
  元件4 = SparkFun Motor Driver TB6612FNG (v11) [part_number=ROB-14451]
  M2 = DC Motor
  R1 = Resistor [tolerance=±5% resistance=220 package=THT]
  LED1 = LED - 5mm [color="Red (633nm)" package="5 mm [THT]"]
  HC-1 = HC-12 Module
  元件6 = Arduino Nano (Rev3.0) (ICSP)
  VCC1 = Battery
  VCC2 = Battery

nets:
  N1: M1.pin_1, 元件4.B01
  N2: M1.pin_2, 元件4.B02
  GND: 元件4.GND, R1.Pin_0, HC-1.GND, 元件6.GND, VCC1.-
  N3: 元件4.A02, M2.pin_1
  N4: 元件4.A01, M2.pin_2
  VCC: 元件4.VCC, HC-1.VCC, 元件6.5V
  N5: 元件4.VM, 元件6.VIN, VCC2.+
  N6: R1.Pin_1, LED1.cathode
  N7: LED1.anode, 元件6.D4
  N8: HC-1.TXD, 元件6.D2
  N9: HC-1.RXD, 元件6.D3

notes:
  1.5V *4 (大電流)
  List:
  Arduino Nano
  TB6612FNG
  LED
  HC-12
  130 Motor
  1.5V Battery
  To Nano Pin:
  HC-12
  TX D2
  RX D3
  LED
  + D4
  - GND
  TB6612FNG
  PWMA D5
  PWMB D6
  AIN1 D7
  AIN2 D8
  BIN1 D9
  BIN2 D10
  STBY 5V
  VCC 5V
  VM 6V
  GND GND
  1.5V*4
  6V VIN

custom parts:
  SparkFun Motor Driver TB6612FNG (v11): The TB6612FNG Motor Driver can control up to two DC motors at a constant current of 1.2A (3.2A peak). Two input signals (IN1 and IN2) can be used to control the motor in one of four function modes: CW, CCW, short-brake and stop. The two motor outputs (A and B) can be separately controlled, and the speed of each motor is controlled via a PWM input signal with a frequency up to 100kHz. The STBY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
  HC-12 Module: HC-12 433Mhz Module

// code stored in the sketch: RemoteControlCar2_TB6612FNG-Fritzing-SLAVE.ino
//Slave

#include <EasyTransfer.h>
#include <SoftwareSerial.h>
SoftwareSerial mySerial(2, 3); //????????? (RX, TX)

int x, y;            // ??x.y?
int checkx, checky;  // ??x.y?
int delaytime = 10;  // ????
long LastTime;       // ??????????????
long Interval = 500; // ??????????????

//create object
EasyTransfer ET;

struct RECEIVE_DATA_STRUCTURE {
  //put your variable definitions here for the data you want to receive
  //THIS MUST BE EXACTLY THE SAME ON THE OTHER ARDUINO
  int16_t gox;
  int16_t goy;
};

//give a name to the group of data
RECEIVE_DATA_STRUCTURE mydata;

void setup() {
  Serial.begin(2400);    // ???????
  mySerial.begin(2400);  // ??HC-12?????

  ET.begin(details(mydata), &mySerial);  // ??EasyTransfer

  pinMode(4, OUTPUT);     // LED?
  //????
  pinMode(5, OUTPUT);     // PWMA
  pinMode(7, OUTPUT);     // AIN1
  pinMode(8, OUTPUT);     // AIN2
  //???
  pinMode(6, OUTPUT);     // PWMB
  pinMode(9, OUTPUT);     // BIN1
  pinMode(10, OUTPUT);    // BIN2

  digitalWrite(4, LOW);   // LED?
  digitalWrite(7, LOW);   // AIN1
  digitalWrite(8, LOW);   // AIN2
  digitalWrite(9, LOW);   // BIN1
  digitalWrite(10, LOW);  // BIN2
}

void loop() {
  if (ET.receiveData()) {        // ??ET????
    x = mydata.gox;              // ? mydata??gox??x
    y = mydata.goy;              // ? mydata??goy??y
    //Serial.println(x);
    //Serial.println(y);

    if (x <= 30 && x >= (-30)) {   // x??30??-30
      analogWrite(5, 0);
      digitalWrite(4, LOW);
      digitalWrite(7, LOW);
      digitalWrite(8, LOW);
      delay(delaytime);
    }
    if (x >= 30) {                 // x??30 checkx??x?
      digitalWrite(4, HIGH);
      digitalWrite(7, HIGH);
      digitalWrite(8, LOW);
      checkx = x;
      analogWrite(5, checkx);
      delay(delaytime);
    }
    if (x <= (-30)) {              // x??-30 checkx??x????
      digitalWrite(4, HIGH);
      digitalWrite(7, LOW);
      digitalWrite(8, HIGH);
      checkx = abs(x);
      analogWrite(5, checkx);
      delay(delaytime);
    }

    if (y <= 30 && y >= (-30)) {   // y??30??-30
      analogWrite(6, 0);
      digitalWrite(4, LOW);
      digitalWrite(9, LOW);
      digitalWrite(10, LOW);
      delay(delaytime);
    }
    if (y >= 30) {                 // y??30 checky??y?
      digitalWrite(4, HIGH);
      digitalWrite(9, HIGH);
      digitalWrite(10, LOW);
      checky = y;
      analogWrite(6, checky);
      delay(delaytime);
    }
    if (y <= (-30)) {              // y??-30 checky??y????
      digitalWrite(4, HIGH);
      digitalWrite(9, LOW);
      digitalWrite(10, HIGH);
      checky = abs(y);
      analogWrite(6, checky);
      delay(delaytime);
    }
    LastTime = millis();
  }
  
  if ((millis() - LastTime) >= Interval) {
    digitalWrite(4, HIGH);   // LED?
    digitalWrite(7, LOW);    // AIN1
    digitalWrite(8, LOW);    // AIN2
    digitalWrite(9, LOW);    // BIN1
    digitalWrite(10, LOW);   // BIN2
  }
}
