# Fritzing sketch RemoteControlCar3-Master (saved by Fritzing 0.9.9b)
breadboards: 1

parts:
  HC-1 = HC-12 Module
  元件1 = Thumb Joystick
  元件2 = Thumb Joystick
  元件3 = Arduino Nano (Rev3.0) (ICSP)  # not connected
  U1 = LIPO-1000mAh [package=lipo-1000]  # not connected

nets:
  GND: HC-1.GND, 元件1.GND, 元件2.GND
  VCC: HC-1.VCC, 元件1.VCC, 元件2.VCC

notes:
  Forward. Backward
  X axis
  Right. Left
  Y axis
  3.7V (3V) to 5V converter
  List:
  Arduino Nano
  Hc-12
  JoyStick
  Converter
  1.5V Battery
  To Nano Pin:
  Hc-12
  TX D2
  RX D3
  VCC 5V
  GND GND
  JoyStick
  X axis A0
  Y axis A1
  VCC 5V
  GND GND
  Converter
  + VIN or 5V
  GND GND

custom parts:
  HC-12 Module: HC-12 433Mhz Module

// code stored in the sketch: Untitled.ino
//Master

#include <EasyTransfer.h>
#include <SoftwareSerial.h>
SoftwareSerial mySerial(2, 3); //????????? (RX, TX)

int x, y;
int checkx, checky;

//create object
EasyTransfer ET;

struct SEND_DATA_STRUCTURE {
  //put your variable definitions here for the data you want to send
  //THIS MUST BE EXACTLY THE SAME ON THE OTHER ARDUINO
  int16_t gox;
  int16_t goy;
};

//give a name to the group of data
SEND_DATA_STRUCTURE mydata;

void setup() {
  Serial.begin(2400);
  mySerial.begin(2400);
  //start the library, pass in the data details and the name of the serial port. Can be Serial, Serial1, Serial2, etc.
  ET.begin(details(mydata), &mySerial);
}

void loop() {
  x = analogRead(A0);
  y = analogRead(A1);


  mydata.gox = map(x, 0, 1023, -255, 255);
  mydata.goy = map(y, 0, 1023, 255, -255);

  ET.sendData();
  checkx = x;
  checky = y;

  Serial.println(x);
  Serial.println(y);
  delay(30);
}
