# Fritzing sketch RemoteControlCar3_TB6612FNG-SLAVE-Ori (saved by Fritzing 0.9.9b)
circuit board: 5.09896cm x 5.35285cm
breadboards: 1

parts:
  M1 = DC Motor
  TB6612FNG = SparkFun Motor Driver TB6612FNG (v11) [part_number=ROB-14451]
  R1 = Resistor [tolerance=±5% resistance=220 power=0.25 package=THT]
  LED1 = LED - 5mm [color="Red (633nm)" current=0.030 package="5 mm [THT]"]
  Arduino_Nano = Arduino Nano (Rev3.0) (ICSP)
  Vin = Battery
  M2 = DC Motor
  HC-12 = female pin header, 5 pins [form="♀ (female)"]

nets:
  N1: M1.pin_1, TB6612FNG.A02
  N2: M1.pin_2, TB6612FNG.A01
  GND: TB6612FNG.GND, R1.Pin_1, Arduino_Nano.GND, Vin.-, HC-12.pin4
  N3: TB6612FNG.B01, M2.pin_1
  N4: TB6612FNG.B02, M2.pin_2
  VCC: TB6612FNG.VCC, TB6612FNG.STBY, Arduino_Nano.5V, HC-12.pin5
  N5: TB6612FNG.VM, Arduino_Nano.VIN, Vin.+
  N6: TB6612FNG.PWMA, Arduino_Nano.D5
  N7: TB6612FNG.AIN2, Arduino_Nano.D10
  N8: TB6612FNG.AIN1, Arduino_Nano.D9
  N9: TB6612FNG.BIN1, Arduino_Nano.D8
  N10: TB6612FNG.BIN2, Arduino_Nano.D7
  N11: TB6612FNG.PWMB, Arduino_Nano.D6
  N12: R1.Pin_0, LED1.cathode
  N13: LED1.anode, Arduino_Nano.D4
  N14: Arduino_Nano.D2, HC-12.pin2
  N15: Arduino_Nano.D3, HC-12.pin3
  N16: Arduino_Nano.D11/MOSI, HC-12.pin1

notes:
  1.5V *4 (大電流)
  List:
  Arduino Nano
  TB6612FNG
  LED
  HC-12
  130 Motor
  1.5V Battery
  To Nano Pin:
  HC-12
  TX D2
  RX D3
  SET D11
  LED
  + D4
  - GND
  TB6612FNG
  PWMA D5
  PWMB D6
  AIN1 D9
  AIN2 D10
  BIN1 D8
  BIN2 D7
  STBY 5V
  VCC 5V
  VM 6V
  GND GND
  1.5V*4
  6V VIN

custom parts:
  SparkFun Motor Driver TB6612FNG (v11): The TB6612FNG Motor Driver can control up to two DC motors at a constant current of 1.2A (3.2A peak). Two input signals (IN1 and IN2) can be used to control the motor in one of four function modes: CW, CCW, short-brake and stop. The two motor outputs (A and B) can be separately controlled, and the speed of each motor is controlled via a PWM input signal with a frequency up to 100kHz. The STBY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

// code stored in the sketch: RemoteControlCar2_TB6612FNG-Fritzing-SLAVE.ino
//Slave

#include <EasyTransfer.h>
#include <SoftwareSerial.h>
SoftwareSerial mySerial(2, 3); //????????? (RX, TX)

int x, y;            // ??x.y?
int checkx, checky;  // ??x.y?
int delaytime = 10;  // ????
long LastTime;       // ??????????????
long Interval = 500; // ??????????????

//create object
EasyTransfer ET;

struct RECEIVE_DATA_STRUCTURE {
  //put your variable definitions here for the data you want to receive
  //THIS MUST BE EXACTLY THE SAME ON THE OTHER ARDUINO
  int16_t gox;
  int16_t goy;
};

//give a name to the group of data
RECEIVE_DATA_STRUCTURE mydata;

void setup() {
  Serial.begin(2400);    // ???????
  mySerial.begin(2400);  // ??HC-12?????

  ET.begin(details(mydata), &mySerial);  // ??EasyTransfer

  pinMode(4, OUTPUT);     // LED?
  //????
  pinMode(5, OUTPUT);     // PWMA
  pinMode(7, OUTPUT);     // AIN1
  pinMode(8, OUTPUT);     // AIN2
  //???
  pinMode(6, OUTPUT);     // PWMB
  pinMode(9, OUTPUT);     // BIN1
  pinMode(10, OUTPUT);    // BIN2

  digitalWrite(4, LOW);   // LED?
  digitalWrite(7, LOW);   // AIN1
  digitalWrite(8, LOW);   // AIN2
  digitalWrite(9, LOW);   // BIN1
  digitalWrite(10, LOW);  // BIN2
}

void loop() {
  if (ET.receiveData()) {        // ??ET????
    x = mydata.gox;              // ? mydata??gox??x
    y = mydata.goy;              // ? mydata??goy??y
    //Serial.println(x);
    //Serial.println(y);

    if (x <= 30 && x >= (-30)) {   // x??30??-30
      analogWrite(5, 0);
      digitalWrite(4, LOW);
      digitalWrite(7, LOW);
      digitalWrite(8, LOW);
      delay(delaytime);
    }
    if (x >= 30) {                 // x??30 checkx??x?
      digitalWrite(4, HIGH);
      digitalWrite(7, HIGH);
      digitalWrite(8, LOW);
      checkx = x;
      analogWrite(5, checkx);
      delay(delaytime);
    }
    if (x <= (-30)) {              // x??-30 checkx??x????
      digitalWrite(4, HIGH);
      digitalWrite(7, LOW);
      digitalWrite(8, HIGH);
      checkx = abs(x);
      analogWrite(5, checkx);
      delay(delaytime);
    }

    if (y <= 30 && y >= (-30)) {   // y??30??-30
      analogWrite(6, 0);
      digitalWrite(4, LOW);
      digitalWrite(9, LOW);
      digitalWrite(10, LOW);
      delay(delaytime);
    }
    if (y >= 30) {                 // y??30 checky??y?
      digitalWrite(4, HIGH);
      digitalWrite(9, HIGH);
      digitalWrite(10, LOW);
      checky = y;
      analogWrite(6, checky);
      delay(delaytime);
    }
    if (y <= (-30)) {              // y??-30 checky??y????
      digitalWrite(4, HIGH);
      digitalWrite(9, LOW);
      digitalWrite(10, HIGH);
      checky = abs(y);
      analogWrite(6, checky);
      delay(delaytime);
    }
    LastTime = millis();
  }
  
  if ((millis() - LastTime) >= Interval) {
    digitalWrite(4, HIGH);   // LED?
    digitalWrite(7, LOW);    // AIN1
    digitalWrite(8, LOW);    // AIN2
    digitalWrite(9, LOW);    // BIN1
    digitalWrite(10, LOW);   // BIN2
  }
}
