# Fritzing sketch RemoteControlCar3_TB6612FNG-SLAVE (saved by Fritzing 0.9.9b)
breadboards: 1

parts:
  Moto1 = DC Motor
  TB6612FNG = SparkFun Motor Driver TB6612FNG (v11) [part_number=ROB-14451]
  Moto2 = DC Motor
  R1 = Resistor [tolerance=±5% resistance=220 power=0.25 package=THT]
  LED1 = LED - 5mm [color="Red (633nm)" current=0.030 package="5 mm [THT]"]
  HC-12 = HC-12 Module
  Arduino_Nano = Arduino Nano (Rev3.0) (ICSP)
  VCC2 = Battery

nets:
  N1: Moto1.pin_1, TB6612FNG.B01
  N2: Moto1.pin_2, TB6612FNG.B02
  GND: TB6612FNG.GND, R1.Pin_0, HC-12.GND, Arduino_Nano.GND, VCC2.-
  N3: TB6612FNG.A02, Moto2.pin_1
  N4: TB6612FNG.A01, Moto2.pin_2
  VCC: TB6612FNG.VCC, TB6612FNG.STBY, HC-12.VCC, Arduino_Nano.5V
  N5: TB6612FNG.VM, Arduino_Nano.VIN, VCC2.+
  N6: TB6612FNG.PWMA, Arduino_Nano.D5
  N7: TB6612FNG.AIN2, Arduino_Nano.D8
  N8: TB6612FNG.AIN1, Arduino_Nano.D7
  N9: TB6612FNG.BIN1, Arduino_Nano.D9
  N10: TB6612FNG.BIN2, Arduino_Nano.D10
  N11: TB6612FNG.PWMB, Arduino_Nano.D6
  N12: R1.Pin_1, LED1.cathode
  N13: LED1.anode, Arduino_Nano.D4
  N14: HC-12.TXD, Arduino_Nano.D2
  N15: HC-12.RXD, Arduino_Nano.D3

notes:
  3.7V*2 (18650)
  List:
  Arduino Nano
  TB6612FNG
  LED
  HC-12
  130 Motor
  1.5V Battery
  To Nano Pin:
  HC-12
  TX D2
  RX D3
  LED
  + D4
  - GND
  TB6612FNG
  PWMA D5
  PWMB D6
  AIN1 D7
  AIN2 D8
  BIN1 D9
  BIN2 D10
  STBY 5V
  VCC 5V
  VM 6V
  GND GND
  3.7V*2 (18650)
  7.4V VIN

custom parts:
  SparkFun Motor Driver TB6612FNG (v11): The TB6612FNG Motor Driver can control up to two DC motors at a constant current of 1.2A (3.2A peak). Two input signals (IN1 and IN2) can be used to control the motor in one of four function modes: CW, CCW, short-brake and stop. The two motor outputs (A and B) can be separately controlled, and the speed of each motor is controlled via a PWM input signal with a frequency up to 100kHz. The STBY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
  HC-12 Module: HC-12 433Mhz Module

// code stored in the sketch: RemoteControlCar2_TB6612FNG-Fritzing-SLAVE.ino
//Slave

#include <EasyTransfer.h>
#include <SoftwareSerial.h>
SoftwareSerial mySerial(2, 3); //????????? (RX, TX)

int x, y;            // ??x.y?
int checkx, checky;  // ??x.y?
int delaytime = 10;  // ????
long LastTime;       // ??????????????
long Interval = 500; // ??????????????

//create object
EasyTransfer ET;

struct RECEIVE_DATA_STRUCTURE {
  //put your variable definitions here for the data you want to receive
  //THIS MUST BE EXACTLY THE SAME ON THE OTHER ARDUINO
  int16_t gox;
  int16_t goy;
};

//give a name to the group of data
RECEIVE_DATA_STRUCTURE mydata;

void setup() {
  Serial.begin(2400);    // ???????
  mySerial.begin(2400);  // ??HC-12?????

  ET.begin(details(mydata), &mySerial);  // ??EasyTransfer

  pinMode(4, OUTPUT);     // LED?
  //????
  pinMode(5, OUTPUT);     // PWMA
  pinMode(7, OUTPUT);     // AIN1
  pinMode(8, OUTPUT);     // AIN2
  //???
  pinMode(6, OUTPUT);     // PWMB
  pinMode(9, OUTPUT);     // BIN1
  pinMode(10, OUTPUT);    // BIN2

  digitalWrite(4, LOW);   // LED?
  digitalWrite(7, LOW);   // AIN1
  digitalWrite(8, LOW);   // AIN2
  digitalWrite(9, LOW);   // BIN1
  digitalWrite(10, LOW);  // BIN2
}

void loop() {
  if (ET.receiveData()) {        // ??ET????
    x = mydata.gox;              // ? mydata??gox??x
    y = mydata.goy;              // ? mydata??goy??y
    //Serial.println(x);
    //Serial.println(y);

    if (x <= 30 && x >= (-30)) {   // x??30??-30
      analogWrite(5, 0);
      digitalWrite(4, LOW);
      digitalWrite(7, LOW);
      digitalWrite(8, LOW);
      delay(delaytime);
    }
    if (x >= 30) {                 // x??30 checkx??x?
      digitalWrite(4, HIGH);
      digitalWrite(7, HIGH);
      digitalWrite(8, LOW);
      checkx = x;
      analogWrite(5, checkx);
      delay(delaytime);
    }
    if (x <= (-30)) {              // x??-30 checkx??x????
      digitalWrite(4, HIGH);
      digitalWrite(7, LOW);
      digitalWrite(8, HIGH);
      checkx = abs(x);
      analogWrite(5, checkx);
      delay(delaytime);
    }

    if (y <= 30 && y >= (-30)) {   // y??30??-30
      analogWrite(6, 0);
      digitalWrite(4, LOW);
      digitalWrite(9, LOW);
      digitalWrite(10, LOW);
      delay(delaytime);
    }
    if (y >= 30) {                 // y??30 checky??y?
      digitalWrite(4, HIGH);
      digitalWrite(9, HIGH);
      digitalWrite(10, LOW);
      checky = y;
      analogWrite(6, checky);
      delay(delaytime);
    }
    if (y <= (-30)) {              // y??-30 checky??y????
      digitalWrite(4, HIGH);
      digitalWrite(9, LOW);
      digitalWrite(10, HIGH);
      checky = abs(y);
      analogWrite(6, checky);
      delay(delaytime);
    }
    LastTime = millis();
  }
  
  if ((millis() - LastTime) >= Interval) {
    digitalWrite(4, HIGH);   // LED?
    digitalWrite(7, LOW);    // AIN1
    digitalWrite(8, LOW);    // AIN2
    digitalWrite(9, LOW);    // BIN1
    digitalWrite(10, LOW);   // BIN2
  }
}
